# Fritzing sketch esp32-FPGA-SID-perfboard (saved by Fritzing 0.9.3b)
circuit board: 8.41071cm x 6.22772cm
perfboards: 1

parts:
  74HC596 = 74HC595 [package="DIP16 [THT]"]
  74HC597 = 74HC595 [package="DIP16 [THT]"]
  SID6581_/_SID6582_/_FPGASID = SID 6581 [package="DIP (Dual Inline) [THT]"]
  12v_Au_Sid_Lat_Clk_Dat_V-_5v = Header 8 [package=1x08_smd]
  C4 = Ceramic Capacitor [capacitance=2.2nF voltage=16V package="100 mil [THT, multilayer]"]
  C3 = Ceramic Capacitor [capacitance=2.2nF voltage=16V package="100 mil [THT, multilayer]"]

nets:
  N1: 74HC596.Q1, SID6581_/_SID6582_/_FPGASID.pin12
  N2: 74HC596.Q2, SID6581_/_SID6582_/_FPGASID.pin11
  N3: 74HC596.Q3, SID6581_/_SID6582_/_FPGASID.pin10
  N4: 74HC596.Q4, SID6581_/_SID6582_/_FPGASID.pin9
  N5: 74HC596.Q5, SID6581_/_SID6582_/_FPGASID.pin8
  N6: 74HC596.Q6, SID6581_/_SID6582_/_FPGASID.pin7
  N7: 74HC596.Q7, SID6581_/_SID6582_/_FPGASID.pin5
  GND: 74HC596.GND, 74HC596.OE, 74HC597.GND, 74HC597.OE, SID6581_/_SID6582_/_FPGASID.pin14, 12v_Au_Sid_Lat_Clk_Dat_V-_5v.1
  VCC: 74HC596.MR, 74HC596.VCC, 74HC597.MR, 74HC597.VCC, SID6581_/_SID6582_/_FPGASID.pin25, 12v_Au_Sid_Lat_Clk_Dat_V-_5v.2
  N8: 74HC596.SH_CP, 74HC597.SH_CP, 12v_Au_Sid_Lat_Clk_Dat_V-_5v.4
  N9: 74HC596.ST_CP, 74HC597.ST_CP, 12v_Au_Sid_Lat_Clk_Dat_V-_5v.5
  N10: 74HC596.DS, 74HC597.Q7'
  N11: 74HC596.Q0, SID6581_/_SID6582_/_FPGASID.pin13
  N12: 74HC597.Q1, SID6581_/_SID6582_/_FPGASID.pin21
  N13: 74HC597.Q2, SID6581_/_SID6582_/_FPGASID.pin20
  N14: 74HC597.Q3, SID6581_/_SID6582_/_FPGASID.pin19
  N15: 74HC597.Q4, SID6581_/_SID6582_/_FPGASID.pin18
  N16: 74HC597.Q5, SID6581_/_SID6582_/_FPGASID.pin17
  N17: 74HC597.Q6, SID6581_/_SID6582_/_FPGASID.pin16
  N18: 74HC597.Q7, SID6581_/_SID6582_/_FPGASID.pin15
  N19: 74HC597.DS, 12v_Au_Sid_Lat_Clk_Dat_V-_5v.3
  N20: 74HC597.Q0, SID6581_/_SID6582_/_FPGASID.pin22
  N21: SID6581_/_SID6582_/_FPGASID.pin1, C4.1
  N22: SID6581_/_SID6582_/_FPGASID.pin2, C4.0
  N23: SID6581_/_SID6582_/_FPGASID.pin3, C3.1
  N24: SID6581_/_SID6582_/_FPGASID.pin4, C3.0
  N25: SID6581_/_SID6582_/_FPGASID.pin6, 12v_Au_Sid_Lat_Clk_Dat_V-_5v.6
  N26: SID6581_/_SID6582_/_FPGASID.pin27, 12v_Au_Sid_Lat_Clk_Dat_V-_5v.7
  N27: SID6581_/_SID6582_/_FPGASID.pin28, 12v_Au_Sid_Lat_Clk_Dat_V-_5v.8

custom parts:
  SID 6581: C64 SID 6581
